// Logisim project SequentialMultiplier.circ as structural Verilog: 5 circuits, main circuit Multiplier
module Multiplier (
  input  [7:0] A,
  input  [7:0] B,
  input  START,
  output DONE,
  output [15:0] PRODUCT
);

  wire and_1_out, clock_1_out, LOAD_B_lsb, not_1_out;
  wire [15:0] LOAD_A_shifted_a;

  Clock clock_1 (.out(clock_1_out));
  and and_1 (and_1_out, clock_1_out, not_1_out);
  not not_1 (not_1_out, DONE);
  LoadA LOAD_A (.C(and_1_out), .A(A), .start(START), .shifted_A(LOAD_A_shifted_a));
  // Probe on LOAD_A_shifted_a
  Computation Computation (
    .shifted_A(LOAD_A_shifted_a), .LSB(LOAD_B_lsb), .C(clock_1_out), .Start(START), .product(PRODUCT),
    .Done(DONE));
  LoadB LOAD_B (.B(B), .C(and_1_out), .Start(START), .LSB(LOAD_B_lsb));
  // Probe on LOAD_B_lsb

  // Notes on the sheet:
  //   Duan Li, 260683698
endmodule

module shiftLeftReg (
  input  C,
  input  A0,
  input  A1,
  input  A2,
  input  A3,
  input  A4,
  input  A5,
  input  A6,
  input  A7,
  input  A8,
  input  A9,
  input  A10,
  input  A11,
  input  A12,
  input  A13,
  input  A14,
  input  A15,
  input  Write_Signal,
  output Q15,
  output Q0,
  output Q1,
  output Q2,
  output Q3,
  output Q4,
  output Q5,
  output Q6,
  output Q7,
  output Q8,
  output Q9,
  output Q10,
  output Q11,
  output Q12,
  output Q13,
  output Q14
);

  wire multiplexer_1_out, multiplexer_2_out, multiplexer_3_out, multiplexer_4_out, multiplexer_5_out,
       multiplexer_6_out, multiplexer_7_out, multiplexer_8_out, multiplexer_9_out, multiplexer_10_out,
       multiplexer_11_out, multiplexer_12_out, multiplexer_13_out, multiplexer_14_out, multiplexer_15_out,
       multiplexer_16_out;

  Multiplexer multiplexer_1 (.in0(1'b0), .in1(A0), .out(multiplexer_1_out), .sel(Write_Signal));  // open: en
  D_Flip_Flop d_ff_1 (.clk(C), .D(multiplexer_1_out), .Q(Q0));  // open: Qn, preset, en, reset
  D_Flip_Flop d_ff_2 (.clk(C), .D(multiplexer_2_out), .Q(Q1));  // open: Qn, preset, en, reset
  Multiplexer multiplexer_2 (.in0(Q0), .in1(A1), .out(multiplexer_2_out), .sel(Write_Signal));  // open: en
  Multiplexer multiplexer_3 (.in0(Q1), .in1(A2), .out(multiplexer_3_out), .sel(Write_Signal));  // open: en
  D_Flip_Flop d_ff_3 (.clk(C), .D(multiplexer_3_out), .Q(Q2));  // open: Qn, preset, en, reset
  D_Flip_Flop d_ff_4 (.clk(C), .D(multiplexer_4_out), .Q(Q3));  // open: Qn, preset, en, reset
  Multiplexer multiplexer_4 (.in0(Q2), .in1(A3), .out(multiplexer_4_out), .sel(Write_Signal));  // open: en
  Multiplexer multiplexer_5 (.in0(Q3), .in1(A4), .out(multiplexer_5_out), .sel(Write_Signal));  // open: en
  D_Flip_Flop d_ff_5 (.clk(C), .D(multiplexer_5_out), .Q(Q4));  // open: Qn, preset, en, reset
  D_Flip_Flop d_ff_6 (.clk(C), .D(multiplexer_6_out), .Q(Q5));  // open: Qn, preset, en, reset
  Multiplexer multiplexer_6 (.in0(Q4), .in1(A5), .out(multiplexer_6_out), .sel(Write_Signal));  // open: en
  Multiplexer multiplexer_7 (.in0(Q5), .in1(A6), .out(multiplexer_7_out), .sel(Write_Signal));  // open: en
  D_Flip_Flop d_ff_7 (.clk(C), .D(multiplexer_7_out), .Q(Q6));  // open: Qn, preset, en, reset
  D_Flip_Flop d_ff_8 (.clk(C), .D(multiplexer_8_out), .Q(Q7));  // open: Qn, preset, en, reset
  Multiplexer multiplexer_8 (.in0(Q6), .in1(A7), .out(multiplexer_8_out), .sel(Write_Signal));  // open: en
  Multiplexer multiplexer_9 (.in0(Q7), .in1(A8), .out(multiplexer_9_out), .sel(Write_Signal));  // open: en
  D_Flip_Flop d_ff_9 (.clk(C), .D(multiplexer_9_out), .Q(Q8));  // open: Qn, preset, en, reset
  D_Flip_Flop d_ff_10 (.clk(C), .D(multiplexer_10_out), .Q(Q9));  // open: Qn, preset, en, reset
  Multiplexer multiplexer_10 (.in0(Q8), .in1(A9), .out(multiplexer_10_out), .sel(Write_Signal));  // open: en
  Multiplexer multiplexer_11 (.in0(Q9), .in1(A10), .out(multiplexer_11_out), .sel(Write_Signal));  // open: en
  D_Flip_Flop d_ff_11 (.clk(C), .D(multiplexer_11_out), .Q(Q10));  // open: Qn, preset, en, reset
  D_Flip_Flop d_ff_12 (.clk(C), .D(multiplexer_12_out), .Q(Q11));  // open: Qn, preset, en, reset
  Multiplexer multiplexer_12 (.in0(Q10), .in1(A11), .out(multiplexer_12_out), .sel(Write_Signal));  // open: en
  Multiplexer multiplexer_13 (.in0(Q11), .in1(A12), .out(multiplexer_13_out), .sel(Write_Signal));  // open: en
  D_Flip_Flop d_ff_13 (.clk(C), .D(multiplexer_13_out), .Q(Q12));  // open: Qn, preset, en, reset
  D_Flip_Flop d_ff_14 (.clk(C), .D(multiplexer_14_out), .Q(Q13));  // open: Qn, preset, en, reset
  Multiplexer multiplexer_14 (.in0(Q12), .in1(A13), .out(multiplexer_14_out), .sel(Write_Signal));  // open: en
  Multiplexer multiplexer_15 (.in0(Q13), .in1(A14), .out(multiplexer_15_out), .sel(Write_Signal));  // open: en
  D_Flip_Flop d_ff_15 (.clk(C), .D(multiplexer_15_out), .Q(Q14));  // open: Qn, preset, en, reset
  D_Flip_Flop d_ff_16 (.clk(C), .D(multiplexer_16_out), .Q(Q15));  // open: Qn, preset, en, reset
  Multiplexer multiplexer_16 (.in0(Q14), .in1(A15), .out(multiplexer_16_out), .sel(Write_Signal));  // open: en

  // Notes on the sheet:
  //   When write Signal is 1, A is written into the shift left Reg to get prepared to multiplication
endmodule

module LoadA (
  input  C,
  input  [7:0] A,
  input  start,
  output [15:0] shifted_A
);

  wire [15:0] bit_extender_1_out;

  assign bit_extender_1_out = {{8{1'b0}}, A};  // Bit_Extender bit_extender_1
  shiftLeftReg shiftleftreg_1 (
    .C(C), .A0(bit_extender_1_out[0]), .A1(bit_extender_1_out[1]), .A2(bit_extender_1_out[2]),
    .A3(bit_extender_1_out[3]), .A4(bit_extender_1_out[4]), .A5(bit_extender_1_out[5]),
    .A6(bit_extender_1_out[6]), .A7(bit_extender_1_out[7]), .A8(bit_extender_1_out[8]),
    .A9(bit_extender_1_out[9]), .A10(bit_extender_1_out[10]), .A11(bit_extender_1_out[11]),
    .A12(bit_extender_1_out[12]), .A13(bit_extender_1_out[13]), .A14(bit_extender_1_out[14]),
    .A15(bit_extender_1_out[15]), .Write_Signal(start), .Q15(shifted_A[15]), .Q0(shifted_A[0]),
    .Q1(shifted_A[1]), .Q2(shifted_A[2]), .Q3(shifted_A[3]), .Q4(shifted_A[4]), .Q5(shifted_A[5]),
    .Q6(shifted_A[6]), .Q7(shifted_A[7]), .Q8(shifted_A[8]), .Q9(shifted_A[9]), .Q10(shifted_A[10]),
    .Q11(shifted_A[11]), .Q12(shifted_A[12]), .Q13(shifted_A[13]), .Q14(shifted_A[14]));

  // Notes on the sheet:
  //   extend A into 16-bit number, load it into register when write signal is 1
  //   Write Signal
endmodule

module LoadB (
  input  [7:0] B,
  input  C,
  input  Start,
  output LSB
);

  Shift_Register shiftRightReg (
    .in(1'b0), .clk(C), .out(LSB), .load(Start), .d0(B[7]), .d1(B[6]), .d2(B[5]), .d3(B[4]), .d4(B[3]),
    .d5(B[2]), .d6(B[1]), .d7(B[0]));  // open: shift, clr, q0, q1, q2, q3, q4, q5, q6, q7

  // Notes on the sheet:
  //   Write Signal
endmodule

module Computation (
  input  [15:0] shifted_A,
  input  LSB,
  input  C,
  input  Start,
  output [15:0] product,
  output Done
);

  wire and_1_out, not_1_out;
  wire [15:0] adder_1_out, multiplexer_1_out;

  Multiplexer #(.width(16)) multiplexer_1 (
    .in0({16{1'b0}}), .in1(shifted_A), .out(multiplexer_1_out), .sel(LSB));  // open: en
  Adder #(.width(16)) adder_1 (.a(multiplexer_1_out), .b(product), .out(adder_1_out));  // open: cin, cout
  and and_1 (and_1_out, C, not_1_out);
  Register #(.width(16)) register_1 (.D(adder_1_out), .Q(product), .clk(and_1_out), .clr(Start));  // open: en
  Counter #(.width(4), .max('h8)) counter_1 (.carry(Done), .clk(and_1_out), .clr(Start));  // open: load, D, count, Q
  not not_1 (not_1_out, Done);

  // Notes on the sheet:
  //   If LSB is 1, add shifted A, else, add 0
  //   stop adding after 8 times
endmodule
